// Logisim project Somador_completo_8bits.circ as structural Verilog: 1 circuit, main circuit main
module main (
  input  [7:0] INPUT_TECLADO_1,
  input  [7:0] INPUT_TECLADO_2,
  output out_3,
  output [7:0] Soma
);

  wire main_1_p4, main_2_p4, main_3_p4, main_4_p4, main_5_p4, main_6_p4, main_7_p4;

  // Somador_complemento_main main_1: pin names not known; wires that end beside it: INPUT_TECLADO_1[0], INPUT_TECLADO_2[0], 1'b0, main_1_p4, Soma[0]
  // Somador_complemento_main main_2: pin names not known; wires that end beside it: INPUT_TECLADO_1[1], INPUT_TECLADO_2[1], main_1_p4, main_2_p4, Soma[1]
  // Somador_complemento_main main_3: pin names not known; wires that end beside it: INPUT_TECLADO_1[2], INPUT_TECLADO_2[2], main_2_p4, main_3_p4, Soma[2]
  // Somador_complemento_main main_4: pin names not known; wires that end beside it: INPUT_TECLADO_1[3], INPUT_TECLADO_2[3], main_3_p4, main_4_p4, Soma[3]
  // Somador_complemento_main main_5: pin names not known; wires that end beside it: INPUT_TECLADO_1[4], INPUT_TECLADO_2[4], main_4_p4, main_5_p4, Soma[4]
  // Somador_complemento_main main_6: pin names not known; wires that end beside it: INPUT_TECLADO_1[5], INPUT_TECLADO_2[5], main_5_p4, main_6_p4, Soma[5]
  // Somador_complemento_main main_7: pin names not known; wires that end beside it: INPUT_TECLADO_1[6], INPUT_TECLADO_2[6], main_6_p4, main_7_p4, Soma[6]
  // Somador_complemento_main main_8: pin names not known; wires that end beside it: INPUT_TECLADO_1[7], INPUT_TECLADO_2[7], main_7_p4, out_3, Soma[7]
endmodule
